// Logisim project circuit1a.circ as structural Verilog: 1 circuit, main circuit main
module main (
  input  A,
  input  C,
  input  B,
  output result
);

  wire and_1_out, and_2_out, not_1_out, not_2_out, or_1_out, or_2_out, xor_1_out;

  not not_1 (not_1_out, A);
  not not_2 (not_2_out, C);
  and and_1 (and_1_out, not_1_out, not_2_out);
  and and_2 (and_2_out, C, A);
  xor xor_1 (xor_1_out, C, B);
  or or_1 (or_1_out, and_1_out, B);
  or or_2 (or_2_out, or_1_out, xor_1_out);
  or or_3 (result, or_2_out, and_2_out);
endmodule
