// Logisim project my_adder.circ as structural Verilog: 2 circuits, main circuit main
module main (
  input  sub,
  input  [15:0] A,
  input  [15:0] B,
  output ovf,
  output [15:0] result
);

  wire my_adder_1_c_out, my_adder_2_c_out, my_adder_3_c_out, my_adder_4_c_out, my_adder_5_c_out,
       my_adder_6_c_out, my_adder_7_c_out, my_adder_8_c_out, my_adder_9_c_out, my_adder_10_c_out,
       my_adder_11_c_out, my_adder_12_c_out, my_adder_13_c_out, my_adder_14_c_out, my_adder_15_c_out,
       my_adder_16_c_out, xor_1_out, xor_2_out, xor_3_out, xor_4_out, xor_5_out, xor_6_out, xor_7_out,
       xor_8_out, xor_9_out, xor_10_out, xor_11_out, xor_12_out, xor_13_out, xor_14_out, xor_15_out,
       xor_16_out;

  xor xor_1 (xor_1_out, sub, B[0]);
  my_adder my_adder_1 (.C_in(sub), .A(xor_1_out), .B(A[0]), .Sum(result[0]), .C_out(my_adder_1_c_out));
  xor xor_2 (xor_2_out, sub, B[1]);
  my_adder my_adder_2 (.C_in(my_adder_1_c_out), .A(xor_2_out), .B(A[1]), .Sum(result[1]), .C_out(my_adder_2_c_out));
  xor xor_3 (xor_3_out, sub, B[2]);
  my_adder my_adder_3 (.C_in(my_adder_2_c_out), .A(xor_3_out), .B(A[2]), .Sum(result[2]), .C_out(my_adder_3_c_out));
  xor xor_4 (xor_4_out, sub, B[3]);
  my_adder my_adder_4 (.C_in(my_adder_3_c_out), .A(xor_4_out), .B(A[3]), .Sum(result[3]), .C_out(my_adder_4_c_out));
  xor xor_5 (xor_5_out, sub, B[4]);
  my_adder my_adder_5 (.C_in(my_adder_4_c_out), .A(xor_5_out), .B(A[4]), .Sum(result[4]), .C_out(my_adder_5_c_out));
  xor xor_6 (xor_6_out, sub, B[5]);
  my_adder my_adder_6 (.C_in(my_adder_5_c_out), .A(xor_6_out), .B(A[5]), .Sum(result[5]), .C_out(my_adder_6_c_out));
  xor xor_7 (xor_7_out, sub, B[6]);
  my_adder my_adder_7 (.C_in(my_adder_6_c_out), .A(xor_7_out), .B(A[6]), .Sum(result[6]), .C_out(my_adder_7_c_out));
  xor xor_8 (xor_8_out, sub, B[7]);
  my_adder my_adder_8 (.C_in(my_adder_7_c_out), .A(xor_8_out), .B(A[7]), .Sum(result[7]), .C_out(my_adder_8_c_out));
  xor xor_9 (xor_9_out, sub, B[8]);
  my_adder my_adder_9 (.C_in(my_adder_8_c_out), .A(xor_9_out), .B(A[8]), .Sum(result[8]), .C_out(my_adder_9_c_out));
  xor xor_10 (xor_10_out, sub, B[9]);
  my_adder my_adder_10 (.C_in(my_adder_9_c_out), .A(xor_10_out), .B(A[9]), .Sum(result[9]), .C_out(my_adder_10_c_out));
  xor xor_11 (xor_11_out, sub, B[10]);
  my_adder my_adder_11 (
    .C_in(my_adder_10_c_out), .A(xor_11_out), .B(A[10]), .Sum(result[10]), .C_out(my_adder_11_c_out));
  xor xor_12 (xor_12_out, sub, B[11]);
  my_adder my_adder_12 (
    .C_in(my_adder_11_c_out), .A(xor_12_out), .B(A[11]), .Sum(result[11]), .C_out(my_adder_12_c_out));
  xor xor_13 (xor_13_out, sub, B[12]);
  my_adder my_adder_13 (
    .C_in(my_adder_12_c_out), .A(xor_13_out), .B(A[12]), .Sum(result[12]), .C_out(my_adder_13_c_out));
  xor xor_14 (xor_14_out, sub, B[13]);
  my_adder my_adder_14 (
    .C_in(my_adder_13_c_out), .A(xor_14_out), .B(A[13]), .Sum(result[13]), .C_out(my_adder_14_c_out));
  xor xor_15 (xor_15_out, sub, B[14]);
  my_adder my_adder_15 (
    .C_in(my_adder_14_c_out), .A(xor_15_out), .B(A[14]), .Sum(result[14]), .C_out(my_adder_15_c_out));
  xor xor_16 (xor_16_out, sub, B[15]);
  my_adder my_adder_16 (
    .C_in(my_adder_15_c_out), .A(xor_16_out), .B(A[15]), .Sum(result[15]), .C_out(my_adder_16_c_out));
  xor xor_17 (ovf, my_adder_15_c_out, my_adder_16_c_out);

  // Other names for the same wires on the sheet: s0 = result[0]; s1 = result[1]; s2 = result[2]; s3 = result[3];
  //   s4 = result[4]; s5 = result[5]; s6 = result[6]; s7 = result[7]; s8 = result[8]; s9 = result[9];
  //   s10 = result[10]; s11 = result[11]; s12 = result[12]; s13 = result[13]; s14 = result[14]; s15 = result[15]
endmodule

module my_adder (
  input  C_in,
  input  A,
  input  B,
  output Sum,
  output C_out
);

  wire and_1_out, and_2_out, xor_1_out;

  and and_1 (and_1_out, A, B);
  xor xor_1 (xor_1_out, A, B);
  or or_1 (C_out, and_1_out, and_2_out);
  and and_2 (and_2_out, xor_1_out, C_in);
  xor xor_2 (Sum, C_in, xor_1_out);
endmodule
