// Logisim project robot.circ as structural Verilog: 1 circuit, main circuit main
module main (
  input  in_stopupdown,
  input  in_stopall,
  output out_1D,
  output out_2D,
  output out_tired
);

  wire and_2_out, and_3_out, and_4_out, and_5_out, and_6_out, and_7_out, and_8_out, and_9_out, and_10_out,
       and_11_out, and_12_out, and_13_out, and_14_out, clock, not_1_out, not_2_out, not_3_out, not_4_out,
       not_5_out, not_6_out, not_7_out, not_8_out, not_9_out, not_10_out, not_11_out, not_12_out, not_13_out,
       not_14_out, not_15_out, not_16_out, not_17_out, not_18_out, not_19_out, not_20_out, not_21_out,
       not_22_out, not_23_out, not_24_out, not_25_out, not_26_out, not_27_out, not_28_out, not_29_out,
       not_30_out, not_31_out, not_32_out, not_33_out, not_34_out, not_35_out, not_36_out, not_37_out,
       or_1_out, or_2_out, or_3_out, Q0, Q1, Q2;

  Clock clk (.out(clock));
  not not_1 (not_1_out, Q0);
  not not_2 (not_2_out, Q0);
  not not_3 (not_3_out, in_stopupdown);
  not not_4 (not_4_out, in_stopall);
  not not_5 (not_5_out, Q0);
  not not_6 (not_6_out, Q2);
  not not_7 (not_7_out, in_stopupdown);
  not not_8 (not_8_out, in_stopall);
  not not_9 (not_9_out, Q1);
  not not_10 (not_10_out, Q2);
  not not_11 (not_11_out, in_stopupdown);
  not not_12 (not_12_out, in_stopall);
  not not_13 (not_13_out, Q1);
  not not_14 (not_14_out, Q0);
  not not_15 (not_15_out, Q2);
  not not_16 (not_16_out, in_stopupdown);
  not not_17 (not_17_out, in_stopall);
  not not_18 (not_18_out, Q0);
  not not_19 (not_19_out, in_stopall);
  not not_20 (not_20_out, Q0);
  not not_21 (not_21_out, Q2);
  not not_22 (not_22_out, in_stopall);
  not not_23 (not_23_out, Q1);
  not not_24 (not_24_out, Q2);
  not not_25 (not_25_out, in_stopall);
  not not_26 (not_26_out, Q1);
  not not_27 (not_27_out, Q2);
  not not_28 (not_28_out, in_stopall);
  and and_1 (out_1D, not_1_out, Q2);
  not not_29 (not_29_out, Q0);
  not not_30 (not_30_out, in_stopall);
  and and_2 (and_2_out, not_2_out, Q2, not_3_out, not_4_out);
  and and_3 (and_3_out, not_5_out, Q1, not_6_out, not_7_out, not_8_out);
  and and_4 (and_4_out, not_9_out, Q0, not_10_out, not_11_out, not_12_out);
  and and_5 (and_5_out, not_13_out, not_14_out, not_15_out, not_16_out, not_17_out);
  and and_6 (and_6_out, not_18_out, Q2, in_stopupdown, not_19_out);
  and and_7 (and_7_out, not_20_out, Q1, not_21_out, in_stopupdown, not_22_out);
  and and_8 (and_8_out, not_23_out, Q0, not_24_out, in_stopupdown, not_25_out);
  and and_9 (and_9_out, not_29_out, in_stopupdown, not_30_out);
  and and_10 (and_10_out, not_26_out, Q0, not_27_out, in_stopupdown, not_28_out);
  or or_1 (or_1_out, and_2_out, and_3_out, and_4_out);
  or or_2 (or_2_out, and_5_out, and_6_out, and_7_out, and_8_out);
  D_Flip_Flop D0 (.D(or_1_out), .clk(clock), .Q(Q0));  // open: Qn, preset, reset
  D_Flip_Flop D1 (.D(or_2_out), .clk(clock), .Q(Q1));  // open: Qn, preset, reset
  or or_3 (or_3_out, and_9_out, and_10_out);
  not not_31 (not_31_out, Q0);
  not not_32 (not_32_out, Q2);
  not not_33 (not_33_out, Q1);
  not not_34 (not_34_out, Q2);
  not not_35 (not_35_out, Q0);
  not not_36 (not_36_out, Q1);
  not not_37 (not_37_out, Q2);
  D_Flip_Flop D2 (.D(or_3_out), .clk(clock), .Q(Q2));  // open: Qn, preset, reset
  and and_11 (and_11_out, not_31_out, Q1, not_32_out);
  and and_12 (and_12_out, not_33_out, Q0, not_34_out);
  and and_13 (and_13_out, not_35_out, Q1, Q2);
  and and_14 (and_14_out, not_36_out, Q0, not_37_out);
  or or_4 (out_2D, and_11_out, and_12_out);
  or or_5 (out_tired, and_13_out, and_14_out);

  // Other names for the same wires on the sheet: I0 = in_stopupdown; I1 = in_stopall
endmodule
