// Logisim project cpu.circ as structural Verilog: 11 circuits, main circuit main
module main (
  input  reset
);

  wire add, addi, ALUinB, and_1_out, and_2_out, beqz, blt, BR, clk, DMwe, inputt, j, jal, JP, jr,
       keyboard_1_avail, lw, memory_latch_1_oe_latched, memory_latch_1_we_latched, not_1_out, not_2_out,
       not_3_out, nott, or_9_out, outputt, Rdst, Rwe, slll, srll, sub, xorr, Zero;
  wire [2:0] ALUop, multiplexer_4_out, multiplexer_5_out;
  wire [3:0] Opcode;
  wire [7:0] Keyboard_Data;
  wire [11:0] Address;
  wire [15:0] AddressInput, bit_extender_1_out, bit_extender_2_out, bit_extender_3_out, DataInput, DataOut,
       memory_latch_1_address_latched, memory_latch_1_data_in_latched, multiplexer_1_out, multiplexer_2_out,
       multiplexer_3_out, multiplexer_6_out, multiplexer_7_out, multiplexer_8_out, multiplexer_9_out,
       Read_Value, singleregister_1_out_5, sixteen_bit_adder_1_sum, sixteen_bit_adder_2_sum;

  and and_1 (and_1_out, beqz, Zero);
  or or_1 (BR, and_1_out, and_2_out);
  and and_2 (and_2_out, AddressInput[15], blt);
  or or_2 (JP, j, jr, jal);
  Decoder #(.select(4)) decoder_1 (
    .out0(add), .out1(sub), .out2(addi), .out3(nott), .out4(xorr), .out5(slll), .out6(srll), .out7(lw),
    .out8(DMwe), .out9(beqz), .out10(blt), .out11(j), .out12(jr), .out13(jal), .out14(inputt),
    .out15(outputt), .sel(Opcode));  // open: en
  or or_3 (Rwe, inputt, slll, nott, addi, add, sub, lw, xorr, srll, jal);
  or or_4 (Rdst, slll, sub, nott, inputt, xorr, add, srll);
  or or_5 (ALUop[1], nott, xorr);
  or or_6 (ALUop[0], sub, beqz, blt, xorr, srll);
  or or_7 (ALUop[2], slll, srll);
  or or_8 (ALUinB, DMwe, beqz, lw, addi);
  not not_1 (not_1_out, clk);
  singleRegister singleregister_1 (
    .dataIn(multiplexer_3_out), .clk(not_1_out), .writeEnable(1'b1), .reset(reset),
    .out_5(singleregister_1_out_5));
  not not_2 (not_2_out, clk);
  memory_latch memory_latch_1 (
    .address(AddressInput), .WE(DMwe), .clk(not_2_out), .data_in(DataInput),
    .address_latched(memory_latch_1_address_latched), .WE_latched(memory_latch_1_we_latched),
    .OE_latched(memory_latch_1_oe_latched), .data_in_latched(memory_latch_1_data_in_latched));
  Keyboard keyboard_1 (.clk(not_3_out), .re(inputt), .clr(reset), .avail(keyboard_1_avail), .data(Keyboard_Data[6:0]));
  not not_3 (not_3_out, clk);
  assign bit_extender_1_out = {{10{Address[5]}}, Address[5:0]};  // Bit_Extender bit_extender_1
  not not_4 (Keyboard_Data[7], keyboard_1_avail);
  sixteen_bit_adder sixteen_bit_adder_1 (
    .Sub(1'b0), .A(16'h1), .B(singleregister_1_out_5), .Sum(sixteen_bit_adder_1_sum));  // open: Overflow
  ROM #(.addrWidth(16), .dataWidth(16)) rom_1 (.addr(singleregister_1_out_5), .data({Opcode, Address}));
  RAM #(.addrWidth(16), .dataWidth(16), .trigger("high"), .databus("bibus")) ram_1 (
    .addr(memory_latch_1_address_latched), .we(memory_latch_1_we_latched), .oe(memory_latch_1_oe_latched),
    .din(memory_latch_1_data_in_latched), .dout(DataOut));
  TTY #(.rows(13), .cols(80)) tty_1 (.data(Read_Value[6:0]), .clk(clk), .we(outputt), .clr(reset));
  sixteen_bit_adder sixteen_bit_adder_2 (
    .Sub(1'b0), .A(bit_extender_1_out), .B(sixteen_bit_adder_1_sum), .Sum(sixteen_bit_adder_2_sum));  // open: Overflow
  Multiplexer #(.width(16), .enable("false")) multiplexer_1 (
    .in0(sixteen_bit_adder_1_sum), .in1(sixteen_bit_adder_2_sum), .out(multiplexer_1_out), .sel(BR));
  assign bit_extender_2_out = {{4{Address[11]}}, Address};  // Bit_Extender bit_extender_2
  Multiplexer #(.width(16), .enable("false")) multiplexer_2 (
    .in0(bit_extender_2_out), .in1(Read_Value), .out(multiplexer_2_out), .sel(jr));
  Multiplexer #(.width(16), .enable("false")) multiplexer_3 (
    .in0(multiplexer_1_out), .in1(multiplexer_2_out), .out(multiplexer_3_out), .sel(JP));
  Clock clock_1 (.out(clk));
  Multiplexer #(.width(3), .enable("false")) multiplexer_4 (
    .in0(Address[8:6]), .in1(Address[5:3]), .out(multiplexer_4_out), .sel(Rdst));
  Multiplexer #(.width(3), .enable("false")) multiplexer_5 (
    .in0(multiplexer_4_out), .in1(3'b111), .out(multiplexer_5_out), .sel(jal));
  RegisterFile registerfile_1 (
    .clk(clk), .reset(reset), .WriteData(multiplexer_9_out), .RegWriteEnable(Rwe),
    .WritePort(multiplexer_5_out), .ReadReg1(Address[11:9]), .ReadReg2(Address[8:6]),
    .Reg1Contents(Read_Value), .Reg2Contents(DataInput));
  or or_9 (or_9_out, Read_Value[0], Read_Value[1], Read_Value[2], Read_Value[3], Read_Value[4], Read_Value[5], Read_Value[6], Read_Value[7], Read_Value[8], Read_Value[9], Read_Value[10], Read_Value[11], Read_Value[12], Read_Value[13], Read_Value[14], Read_Value[15]);
  assign bit_extender_3_out = {{10{Address[5]}}, Address[5:0]};  // Bit_Extender bit_extender_3
  not not_5 (Zero, or_9_out);
  Multiplexer #(.width(16), .enable("false")) multiplexer_6 (
    .in0(DataInput), .in1(bit_extender_3_out), .out(multiplexer_6_out), .sel(ALUinB));
  alu alu_1 (
    .InputData1(Read_Value), .InputData2(multiplexer_6_out), .OpType(ALUop), .Shamt(Address[2:0]),
    .OutputData(AddressInput));
  Multiplexer #(.width(16), .enable("false")) multiplexer_7 (
    .in0(AddressInput), .in1(DataOut), .out(multiplexer_7_out), .sel(lw));
  Multiplexer #(.width(16), .enable("false")) multiplexer_8 (
    .in0(multiplexer_7_out), .in1(sixteen_bit_adder_1_sum), .out(multiplexer_8_out), .sel(jal));
  Multiplexer #(.width(16), .enable("false")) multiplexer_9 (
    .in0(multiplexer_8_out), .in1({{8{1'b0}}, Keyboard_Data}), .out(multiplexer_9_out), .sel(inputt));

  // Other names for the same wires on the sheet: Rt[2:0] = Address[8:6]; Rs[2:0] = Address[11:9];
  //   Less_Than = AddressInput[15]; Immediate[5:0] = Address[5:0]; Shamt[2:0] = Address[2:0]; Rd[2:0] = Address[5:3];
  //   sw = DMwe

  // Notes on the sheet:
  //   000: add/addi, 001 sub, 010 not, 011 xor, 100 sll, 101 srl
  //   send data and address here, not directly to RAM
  //   Keyboard
  //   contents of rom_1 (hex, n*v repeats v):
  //   204b 208c 20cc 210d 2141 a446 2142 a4c6 2143 a506 2197 903f 219e 903f 219f 903f 207f 2144 a282 2198
  //   903f 2145 2041 9212 2146 2040 9202 2199 903f 2147 b021 219a 903f 2148 d025 214a 903f 2242 2149 ce00
  //   219b 903f 219c 903f
  //   TTY
endmodule

module singleRegister (
  input  [15:0] dataIn,
  input  clk,
  input  writeEnable,
  input  reset,
  output [15:0] out_5
);

  wire clk_t;

  and and_1 (clk_t, clk, writeEnable);
  D_Flip_Flop d_ff_1 (.D(dataIn[0]), .clk(clk_t), .Q(out_5[0]), .reset(reset));  // open: Qn, preset
  D_Flip_Flop d_ff_2 (.D(dataIn[1]), .clk(clk_t), .Q(out_5[1]), .reset(reset));  // open: Qn, preset
  D_Flip_Flop d_ff_3 (.D(dataIn[2]), .clk(clk_t), .Q(out_5[2]), .reset(reset));  // open: Qn, preset
  D_Flip_Flop d_ff_4 (.D(dataIn[3]), .clk(clk_t), .Q(out_5[3]), .reset(reset));  // open: Qn, preset
  D_Flip_Flop d_ff_5 (.D(dataIn[4]), .clk(clk_t), .Q(out_5[4]), .reset(reset));  // open: Qn, preset
  D_Flip_Flop d_ff_6 (.D(dataIn[5]), .clk(clk_t), .Q(out_5[5]), .reset(reset));  // open: Qn, preset
  D_Flip_Flop d_ff_7 (.D(dataIn[6]), .clk(clk_t), .Q(out_5[6]), .reset(reset));  // open: Qn, preset
  D_Flip_Flop d_ff_8 (.D(dataIn[7]), .clk(clk_t), .Q(out_5[7]), .reset(reset));  // open: Qn, preset
  D_Flip_Flop d_ff_9 (.D(dataIn[8]), .clk(clk_t), .Q(out_5[8]), .reset(reset));  // open: Qn, preset
  D_Flip_Flop d_ff_10 (.D(dataIn[9]), .clk(clk_t), .Q(out_5[9]), .reset(reset));  // open: Qn, preset
  D_Flip_Flop d_ff_11 (.D(dataIn[10]), .clk(clk_t), .Q(out_5[10]), .reset(reset));  // open: Qn, preset
  D_Flip_Flop d_ff_12 (.D(dataIn[11]), .clk(clk_t), .Q(out_5[11]), .reset(reset));  // open: Qn, preset
  D_Flip_Flop d_ff_13 (.D(dataIn[12]), .clk(clk_t), .Q(out_5[12]), .reset(reset));  // open: Qn, preset
  D_Flip_Flop d_ff_14 (.D(dataIn[13]), .clk(clk_t), .Q(out_5[13]), .reset(reset));  // open: Qn, preset
  D_Flip_Flop d_ff_15 (.D(dataIn[14]), .clk(clk_t), .Q(out_5[14]), .reset(reset));  // open: Qn, preset
  D_Flip_Flop d_ff_16 (.D(dataIn[15]), .clk(clk_t), .Q(out_5[15]), .reset(reset));  // open: Qn, preset

  // Other names for the same wires on the sheet: in0 = dataIn[0]; in1 = dataIn[1]; in2 = dataIn[2]; in3 = dataIn[3];
  //   in4 = dataIn[4]; in5 = dataIn[5]; in6 = dataIn[6]; in7 = dataIn[7]; in8 = dataIn[8]; in9 = dataIn[9];
  //   in10 = dataIn[10]; in11 = dataIn[11]; in12 = dataIn[12]; in13 = dataIn[13]; in14 = dataIn[14];
  //   in15 = dataIn[15]; out0 = out_5[0]; out1 = out_5[1]; out2 = out_5[2]; out3 = out_5[3]; out4 = out_5[4];
  //   out5 = out_5[5]; out6 = out_5[6]; out7 = out_5[7]; out8 = out_5[8]; out9 = out_5[9]; out10 = out_5[10];
  //   out11 = out_5[11]; out12 = out_5[12]; out13 = out_5[13]; out14 = out_5[14]; out15 = out_5[15]
endmodule

module RegisterFile (
  input  clk,
  input  reset,
  input  [15:0] WriteData,
  input  RegWriteEnable,
  input  [2:0] WritePort,
  input  [2:0] ReadReg1,
  input  [2:0] ReadReg2,
  output [15:0] Reg1Contents,
  output [15:0] Reg2Contents
);

  wire decoder_1_out0, out1bit0, out1bit1, out1bit2, out1bit3, out1bit4, out1bit5, out1bit6, out1bit7,
       out2bit0, out2bit1, out2bit2, out2bit3, out2bit4, out2bit5, out2bit6, out2bit7, Write1, Write2,
       Write3, Write4, Write5, Write6, Write7;
  wire [15:0] singleregister_1_out_5, singleregister_2_out_5, singleregister_3_out_5, singleregister_4_out_5,
       singleregister_5_out_5, singleregister_6_out_5, singleregister_7_out_5, singleregister_8_out_5;

  Decoder #(.select(3)) decoder_1 (
    .out0(decoder_1_out0), .out1(Write1), .out2(Write2), .out3(Write3), .out4(Write4), .out5(Write5),
    .out6(Write6), .out7(Write7), .sel(WritePort), .en(RegWriteEnable));
  Decoder #(.select(3)) decoder_2 (
    .out0(out1bit0), .out1(out1bit1), .out2(out1bit2), .out3(out1bit3), .out4(out1bit4), .out5(out1bit5),
    .out6(out1bit6), .out7(out1bit7), .sel(ReadReg1));  // open: en
  Decoder #(.select(3)) decoder_3 (
    .out0(out2bit0), .out1(out2bit1), .out2(out2bit2), .out3(out2bit3), .out4(out2bit4), .out5(out2bit5),
    .out6(out2bit6), .out7(out2bit7), .sel(ReadReg2));  // open: en
  // Probe on singleregister_1_out_5
  singleRegister singleregister_1 (
    .dataIn(WriteData), .clk(clk), .writeEnable(1'b0), .reset(reset), .out_5(singleregister_1_out_5));
  // Probe on singleregister_2_out_5
  singleRegister singleregister_2 (
    .dataIn(WriteData), .clk(clk), .writeEnable(Write1), .reset(reset), .out_5(singleregister_2_out_5));
  // Probe on singleregister_3_out_5
  singleRegister singleregister_3 (
    .dataIn(WriteData), .clk(clk), .writeEnable(Write2), .reset(reset), .out_5(singleregister_3_out_5));
  // Probe on singleregister_4_out_5
  singleRegister singleregister_4 (
    .dataIn(WriteData), .clk(clk), .writeEnable(Write3), .reset(reset), .out_5(singleregister_4_out_5));
  // Probe on singleregister_5_out_5
  singleRegister singleregister_5 (
    .dataIn(WriteData), .clk(clk), .writeEnable(Write4), .reset(reset), .out_5(singleregister_5_out_5));
  // Probe on singleregister_6_out_5
  singleRegister singleregister_6 (
    .dataIn(WriteData), .clk(clk), .writeEnable(Write5), .reset(reset), .out_5(singleregister_6_out_5));
  // Probe on singleregister_7_out_5
  singleRegister singleregister_7 (
    .dataIn(WriteData), .clk(clk), .writeEnable(Write6), .reset(reset), .out_5(singleregister_7_out_5));
  // Probe on singleregister_8_out_5
  singleRegister singleregister_8 (
    .dataIn(WriteData), .clk(clk), .writeEnable(Write7), .reset(reset), .out_5(singleregister_8_out_5));
  assign Reg1Contents = out1bit0 ? singleregister_1_out_5 : 16'bz;  // Controlled_Buffer controlled_buffer_1
  assign Reg2Contents = out2bit0 ? singleregister_1_out_5 : 16'bz;  // Controlled_Buffer controlled_buffer_2
  assign Reg1Contents = out1bit1 ? singleregister_2_out_5 : 16'bz;  // Controlled_Buffer controlled_buffer_3
  assign Reg2Contents = out2bit1 ? singleregister_2_out_5 : 16'bz;  // Controlled_Buffer controlled_buffer_4
  assign Reg1Contents = out1bit2 ? singleregister_3_out_5 : 16'bz;  // Controlled_Buffer controlled_buffer_5
  assign Reg2Contents = out2bit2 ? singleregister_3_out_5 : 16'bz;  // Controlled_Buffer controlled_buffer_6
  assign Reg1Contents = out1bit3 ? singleregister_4_out_5 : 16'bz;  // Controlled_Buffer controlled_buffer_7
  assign Reg2Contents = out2bit3 ? singleregister_4_out_5 : 16'bz;  // Controlled_Buffer controlled_buffer_8
  assign Reg1Contents = out1bit4 ? singleregister_5_out_5 : 16'bz;  // Controlled_Buffer controlled_buffer_9
  assign Reg2Contents = out2bit4 ? singleregister_5_out_5 : 16'bz;  // Controlled_Buffer controlled_buffer_10
  assign Reg1Contents = out1bit5 ? singleregister_6_out_5 : 16'bz;  // Controlled_Buffer controlled_buffer_11
  assign Reg2Contents = out2bit5 ? singleregister_6_out_5 : 16'bz;  // Controlled_Buffer controlled_buffer_12
  assign Reg1Contents = out1bit6 ? singleregister_7_out_5 : 16'bz;  // Controlled_Buffer controlled_buffer_13
  assign Reg2Contents = out2bit6 ? singleregister_7_out_5 : 16'bz;  // Controlled_Buffer controlled_buffer_14
  assign Reg1Contents = out1bit7 ? singleregister_8_out_5 : 16'bz;  // Controlled_Buffer controlled_buffer_15
  assign Reg2Contents = out2bit7 ? singleregister_8_out_5 : 16'bz;  // Controlled_Buffer controlled_buffer_16
endmodule

module alu (
  input  [15:0] InputData1,
  input  [15:0] InputData2,
  input  [2:0] OpType,
  input  [2:0] Shamt,
  output [15:0] OutputData
);

  wire [15:0] barrel_shifter_left_1_outputdata, barrel_shifter_right_1_output_data, not_1_out,
       sixteen_bit_adder_1_sum, sixteen_bit_adder_2_sum, xor_1_out;

  assign xor_1_out = InputData2 ^ InputData1;  // XOR_Gate xor_1, 16 bits wide
  assign not_1_out = ~InputData1;  // NOT_Gate not_1, 16 bits wide
  sixteen_bit_adder sixteen_bit_adder_1 (
    .Sub(1'b0), .A(InputData1), .B(InputData2), .Sum(sixteen_bit_adder_1_sum));  // open: Overflow
  sixteen_bit_adder sixteen_bit_adder_2 (
    .Sub(1'b1), .A(InputData1), .B(InputData2), .Sum(sixteen_bit_adder_2_sum));  // open: Overflow
  barrel_shifter_left barrel_shifter_left_1 (
    .Shifter_Input(Shamt), .Input_Data(InputData1), .OutputData(barrel_shifter_left_1_outputdata));
  barrel_shifter_right barrel_shifter_right_1 (
    .in_1(Shamt), .Input_Data(InputData1), .Output_Data(barrel_shifter_right_1_output_data));
  Multiplexer #(.select(3), .width(16), .enable("false")) multiplexer_1 (
    .in0(sixteen_bit_adder_1_sum), .in1(sixteen_bit_adder_2_sum), .in2(not_1_out), .in3(xor_1_out),
    .in4(barrel_shifter_left_1_outputdata), .in5(barrel_shifter_right_1_output_data), .out(OutputData),
    .sel(OpType));  // open: in6, in7
endmodule

module one_bit_adder (
  input  C_in,
  input  A,
  input  B,
  output Sum,
  output C_out
);

  wire and_1_out, and_2_out, xor_1_out;

  and and_1 (and_1_out, A, B);
  xor xor_1 (xor_1_out, A, B);
  or or_1 (C_out, and_1_out, and_2_out);
  and and_2 (and_2_out, xor_1_out, C_in);
  xor xor_2 (Sum, C_in, xor_1_out);
endmodule

module sixteen_bit_adder (
  input  Sub,
  input  [15:0] A,
  input  [15:0] B,
  output Overflow,
  output [15:0] Sum
);

  wire one_bit_adder_1_c_out, one_bit_adder_2_c_out, one_bit_adder_3_c_out, one_bit_adder_4_c_out,
       one_bit_adder_5_c_out, one_bit_adder_6_c_out, one_bit_adder_7_c_out, one_bit_adder_8_c_out,
       one_bit_adder_9_c_out, one_bit_adder_10_c_out, one_bit_adder_11_c_out, one_bit_adder_12_c_out,
       one_bit_adder_13_c_out, one_bit_adder_14_c_out, one_bit_adder_15_c_out, one_bit_adder_16_c_out,
       xor_1_out, xor_2_out, xor_3_out, xor_4_out, xor_5_out, xor_6_out, xor_7_out, xor_8_out, xor_9_out,
       xor_10_out, xor_11_out, xor_12_out, xor_13_out, xor_14_out, xor_15_out, xor_16_out;

  xor xor_1 (xor_1_out, Sub, B[0]);
  one_bit_adder one_bit_adder_1 (.C_in(Sub), .A(xor_1_out), .B(A[0]), .Sum(Sum[0]), .C_out(one_bit_adder_1_c_out));
  xor xor_2 (xor_2_out, Sub, B[1]);
  one_bit_adder one_bit_adder_2 (
    .C_in(one_bit_adder_1_c_out), .A(xor_2_out), .B(A[1]), .Sum(Sum[1]), .C_out(one_bit_adder_2_c_out));
  xor xor_3 (xor_3_out, Sub, B[2]);
  one_bit_adder one_bit_adder_3 (
    .C_in(one_bit_adder_2_c_out), .A(xor_3_out), .B(A[2]), .Sum(Sum[2]), .C_out(one_bit_adder_3_c_out));
  xor xor_4 (xor_4_out, Sub, B[3]);
  one_bit_adder one_bit_adder_4 (
    .C_in(one_bit_adder_3_c_out), .A(xor_4_out), .B(A[3]), .Sum(Sum[3]), .C_out(one_bit_adder_4_c_out));
  xor xor_5 (xor_5_out, Sub, B[4]);
  one_bit_adder one_bit_adder_5 (
    .C_in(one_bit_adder_4_c_out), .A(xor_5_out), .B(A[4]), .Sum(Sum[4]), .C_out(one_bit_adder_5_c_out));
  xor xor_6 (xor_6_out, Sub, B[5]);
  one_bit_adder one_bit_adder_6 (
    .C_in(one_bit_adder_5_c_out), .A(xor_6_out), .B(A[5]), .Sum(Sum[5]), .C_out(one_bit_adder_6_c_out));
  xor xor_7 (xor_7_out, Sub, B[6]);
  one_bit_adder one_bit_adder_7 (
    .C_in(one_bit_adder_6_c_out), .A(xor_7_out), .B(A[6]), .Sum(Sum[6]), .C_out(one_bit_adder_7_c_out));
  xor xor_8 (xor_8_out, Sub, B[7]);
  one_bit_adder one_bit_adder_8 (
    .C_in(one_bit_adder_7_c_out), .A(xor_8_out), .B(A[7]), .Sum(Sum[7]), .C_out(one_bit_adder_8_c_out));
  xor xor_9 (xor_9_out, Sub, B[8]);
  one_bit_adder one_bit_adder_9 (
    .C_in(one_bit_adder_8_c_out), .A(xor_9_out), .B(A[8]), .Sum(Sum[8]), .C_out(one_bit_adder_9_c_out));
  xor xor_10 (xor_10_out, Sub, B[9]);
  one_bit_adder one_bit_adder_10 (
    .C_in(one_bit_adder_9_c_out), .A(xor_10_out), .B(A[9]), .Sum(Sum[9]), .C_out(one_bit_adder_10_c_out));
  xor xor_11 (xor_11_out, Sub, B[10]);
  one_bit_adder one_bit_adder_11 (
    .C_in(one_bit_adder_10_c_out), .A(xor_11_out), .B(A[10]), .Sum(Sum[10]), .C_out(one_bit_adder_11_c_out));
  xor xor_12 (xor_12_out, Sub, B[11]);
  one_bit_adder one_bit_adder_12 (
    .C_in(one_bit_adder_11_c_out), .A(xor_12_out), .B(A[11]), .Sum(Sum[11]), .C_out(one_bit_adder_12_c_out));
  xor xor_13 (xor_13_out, Sub, B[12]);
  one_bit_adder one_bit_adder_13 (
    .C_in(one_bit_adder_12_c_out), .A(xor_13_out), .B(A[12]), .Sum(Sum[12]), .C_out(one_bit_adder_13_c_out));
  xor xor_14 (xor_14_out, Sub, B[13]);
  one_bit_adder one_bit_adder_14 (
    .C_in(one_bit_adder_13_c_out), .A(xor_14_out), .B(A[13]), .Sum(Sum[13]), .C_out(one_bit_adder_14_c_out));
  xor xor_15 (xor_15_out, Sub, B[14]);
  one_bit_adder one_bit_adder_15 (
    .C_in(one_bit_adder_14_c_out), .A(xor_15_out), .B(A[14]), .Sum(Sum[14]), .C_out(one_bit_adder_15_c_out));
  xor xor_16 (xor_16_out, Sub, B[15]);
  one_bit_adder one_bit_adder_16 (
    .C_in(one_bit_adder_15_c_out), .A(xor_16_out), .B(A[15]), .Sum(Sum[15]), .C_out(one_bit_adder_16_c_out));
  xor xor_17 (Overflow, one_bit_adder_15_c_out, one_bit_adder_16_c_out);

  // Other names for the same wires on the sheet: s0 = Sum[0]; s1 = Sum[1]; s2 = Sum[2]; s3 = Sum[3]; s4 = Sum[4];
  //   s5 = Sum[5]; s6 = Sum[6]; s7 = Sum[7]; s8 = Sum[8]; s9 = Sum[9]; s10 = Sum[10]; s11 = Sum[11]; s12 = Sum[12];
  //   s13 = Sum[13]; s14 = Sum[14]; s15 = Sum[15]
endmodule

module memory_latch (
  input  [15:0] address,
  input  WE,
  input  clk,
  input  [15:0] data_in,
  output [15:0] address_latched,
  output WE_latched,
  output OE_latched,
  output [15:0] data_in_latched
);

  wire DMwe_latch_q;
  wire [15:0] addr_latch_q;

  Register #(.width(16), .trigger("falling")) addr_latch (
    .D(address), .en(WE), .clk(clk), .Q(addr_latch_q));  // open: clr
  D_Flip_Flop #(.trigger("falling")) DMwe_latch (.D(WE), .clk(clk), .Q(DMwe_latch_q));  // open: Qn, preset, reset
  Register #(.width(16), .trigger("falling")) data_to_be_written (
    .D(data_in), .en(WE), .clk(clk), .Q(data_in_latched));  // open: clr
  Multiplexer #(.width(16), .enable("false")) multiplexer_1 (
    .in0(address), .in1(addr_latch_q), .out(address_latched), .sel(DMwe_latch_q));
  and and_1 (WE_latched, clk, DMwe_latch_q);
  not not_1 (OE_latched, WE_latched);
endmodule

module barrel_shifter_left (
  input  [2:0] Shifter_Input,
  input  [15:0] Input_Data,
  output [15:0] OutputData
);

  wire [15:0] one_bit_shifter_left_1_output_left, one_bit_shifter_left_2_output_left,
       one_bit_shifter_left_3_output_left, one_bit_shifter_left_4_output_left,
       one_bit_shifter_left_5_output_left, one_bit_shifter_left_7_output_left;

  one_bit_shifter_left one_bit_shifter_left_1 (
    .input_left(Input_Data), .Enable(Shifter_Input[0]), .output_left(one_bit_shifter_left_1_output_left));
  one_bit_shifter_left one_bit_shifter_left_2 (
    .input_left(one_bit_shifter_left_7_output_left), .Enable(Shifter_Input[2]),
    .output_left(one_bit_shifter_left_2_output_left));
  one_bit_shifter_left one_bit_shifter_left_3 (
    .input_left(one_bit_shifter_left_5_output_left), .Enable(Shifter_Input[2]),
    .output_left(one_bit_shifter_left_3_output_left));
  one_bit_shifter_left one_bit_shifter_left_4 (
    .input_left(one_bit_shifter_left_1_output_left), .Enable(Shifter_Input[1]),
    .output_left(one_bit_shifter_left_4_output_left));
  one_bit_shifter_left one_bit_shifter_left_5 (
    .input_left(one_bit_shifter_left_2_output_left), .Enable(Shifter_Input[2]),
    .output_left(one_bit_shifter_left_5_output_left));
  one_bit_shifter_left one_bit_shifter_left_6 (
    .input_left(one_bit_shifter_left_3_output_left), .Enable(Shifter_Input[2]), .output_left(OutputData));
  one_bit_shifter_left one_bit_shifter_left_7 (
    .input_left(one_bit_shifter_left_4_output_left), .Enable(Shifter_Input[1]),
    .output_left(one_bit_shifter_left_7_output_left));

  // Other names for the same wires on the sheet: ShiftEnable1 = Shifter_Input[0]; ShiftEnable2 = Shifter_Input[1];
  //   ShiftEnable4 = Shifter_Input[2]
endmodule

module one_bit_shifter_left (
  input  [15:0] input_left,
  input  Enable,
  output [15:0] output_left
);

  Multiplexer #(.enable("false")) multiplexer_1 (
    .in0(input_left[15]), .in1(input_left[14]), .out(output_left[15]), .sel(Enable));
  Multiplexer #(.enable("false")) multiplexer_2 (
    .in0(input_left[14]), .in1(input_left[13]), .out(output_left[14]), .sel(Enable));
  Multiplexer #(.enable("false")) multiplexer_3 (
    .in0(input_left[13]), .in1(input_left[12]), .out(output_left[13]), .sel(Enable));
  Multiplexer #(.enable("false")) multiplexer_4 (
    .in0(input_left[12]), .in1(input_left[11]), .out(output_left[12]), .sel(Enable));
  Multiplexer #(.enable("false")) multiplexer_5 (
    .in0(input_left[11]), .in1(input_left[10]), .out(output_left[11]), .sel(Enable));
  Multiplexer #(.enable("false")) multiplexer_6 (
    .in0(input_left[10]), .in1(input_left[9]), .out(output_left[10]), .sel(Enable));
  Multiplexer #(.enable("false")) multiplexer_7 (
    .in0(input_left[9]), .in1(input_left[8]), .out(output_left[9]), .sel(Enable));
  Multiplexer #(.enable("false")) multiplexer_8 (
    .in0(input_left[8]), .in1(input_left[7]), .out(output_left[8]), .sel(Enable));
  Multiplexer #(.enable("false")) multiplexer_9 (
    .in0(input_left[7]), .in1(input_left[6]), .out(output_left[7]), .sel(Enable));
  Multiplexer #(.enable("false")) multiplexer_10 (
    .in0(input_left[6]), .in1(input_left[5]), .out(output_left[6]), .sel(Enable));
  Multiplexer #(.enable("false")) multiplexer_11 (
    .in0(input_left[5]), .in1(input_left[4]), .out(output_left[5]), .sel(Enable));
  Multiplexer #(.enable("false")) multiplexer_12 (
    .in0(input_left[4]), .in1(input_left[3]), .out(output_left[4]), .sel(Enable));
  Multiplexer #(.enable("false")) multiplexer_13 (
    .in0(input_left[3]), .in1(input_left[2]), .out(output_left[3]), .sel(Enable));
  Multiplexer #(.enable("false")) multiplexer_14 (
    .in0(input_left[2]), .in1(input_left[1]), .out(output_left[2]), .sel(Enable));
  Multiplexer #(.enable("false")) multiplexer_15 (
    .in0(input_left[1]), .in1(input_left[0]), .out(output_left[1]), .sel(Enable));
  Multiplexer #(.enable("false")) multiplexer_16 (.in0(input_left[0]), .in1(1'b0), .out(output_left[0]), .sel(Enable));

  // Other names for the same wires on the sheet: En = Enable; in0 = input_left[0]; in1 = input_left[1];
  //   in2 = input_left[2]; in3 = input_left[3]; in4 = input_left[4]; in5 = input_left[5]; in6 = input_left[6];
  //   in7 = input_left[7]; in8 = input_left[8]; in9 = input_left[9]; in10 = input_left[10]; in11 = input_left[11];
  //   in12 = input_left[12]; in13 = input_left[13]; in14 = input_left[14]; in15 = input_left[15];
  //   out0 = output_left[0]; out1 = output_left[1]; out2 = output_left[2]; out3 = output_left[3];
  //   out4 = output_left[4]; out5 = output_left[5]; out6 = output_left[6]; out7 = output_left[7];
  //   out8 = output_left[8]; out9 = output_left[9]; out10 = output_left[10]; out11 = output_left[11];
  //   out12 = output_left[12]; out13 = output_left[13]; out14 = output_left[14]; out15 = output_left[15]
endmodule

module one_bit_shifter_right (
  input  [15:0] in_1,
  input  in_2,
  output [15:0] out_3
);

  Multiplexer #(.enable("false")) multiplexer_1 (.in0(in_1[0]), .in1(in_1[1]), .out(out_3[0]), .sel(in_2));
  Multiplexer #(.enable("false")) multiplexer_2 (.in0(in_1[1]), .in1(in_1[2]), .out(out_3[1]), .sel(in_2));
  Multiplexer #(.enable("false")) multiplexer_3 (.in0(in_1[2]), .in1(in_1[3]), .out(out_3[2]), .sel(in_2));
  Multiplexer #(.enable("false")) multiplexer_4 (.in0(in_1[3]), .in1(in_1[4]), .out(out_3[3]), .sel(in_2));
  Multiplexer #(.enable("false")) multiplexer_5 (.in0(in_1[4]), .in1(in_1[5]), .out(out_3[4]), .sel(in_2));
  Multiplexer #(.enable("false")) multiplexer_6 (.in0(in_1[5]), .in1(in_1[6]), .out(out_3[5]), .sel(in_2));
  Multiplexer #(.enable("false")) multiplexer_7 (.in0(in_1[6]), .in1(in_1[7]), .out(out_3[6]), .sel(in_2));
  Multiplexer #(.enable("false")) multiplexer_8 (.in0(in_1[7]), .in1(in_1[8]), .out(out_3[7]), .sel(in_2));
  Multiplexer #(.enable("false")) multiplexer_9 (.in0(in_1[8]), .in1(in_1[9]), .out(out_3[8]), .sel(in_2));
  Multiplexer #(.enable("false")) multiplexer_10 (.in0(in_1[9]), .in1(in_1[10]), .out(out_3[9]), .sel(in_2));
  Multiplexer #(.enable("false")) multiplexer_11 (.in0(in_1[10]), .in1(in_1[11]), .out(out_3[10]), .sel(in_2));
  Multiplexer #(.enable("false")) multiplexer_12 (.in0(in_1[11]), .in1(in_1[12]), .out(out_3[11]), .sel(in_2));
  Multiplexer #(.enable("false")) multiplexer_13 (.in0(in_1[12]), .in1(in_1[13]), .out(out_3[12]), .sel(in_2));
  Multiplexer #(.enable("false")) multiplexer_14 (.in0(in_1[13]), .in1(in_1[14]), .out(out_3[13]), .sel(in_2));
  Multiplexer #(.enable("false")) multiplexer_15 (.in0(in_1[14]), .in1(in_1[15]), .out(out_3[14]), .sel(in_2));
  Multiplexer #(.enable("false")) multiplexer_16 (.in0(in_1[15]), .in1(1'b0), .out(out_3[15]), .sel(in_2));

  // Other names for the same wires on the sheet: En = in_2; in0 = in_1[0]; in1 = in_1[1]; in2 = in_1[2];
  //   in3 = in_1[3]; in4 = in_1[4]; in5 = in_1[5]; in6 = in_1[6]; in7 = in_1[7]; in8 = in_1[8]; in9 = in_1[9];
  //   in10 = in_1[10]; in11 = in_1[11]; in12 = in_1[12]; in13 = in_1[13]; in14 = in_1[14]; in15 = in_1[15];
  //   out0 = out_3[0]; out1 = out_3[1]; out2 = out_3[2]; out3 = out_3[3]; out4 = out_3[4]; out5 = out_3[5];
  //   out6 = out_3[6]; out7 = out_3[7]; out8 = out_3[8]; out9 = out_3[9]; out10 = out_3[10]; out11 = out_3[11];
  //   out12 = out_3[12]; out13 = out_3[13]; out14 = out_3[14]; out15 = out_3[15]
endmodule

module barrel_shifter_right (
  input  [2:0] in_1,
  input  [15:0] Input_Data,
  output [15:0] Output_Data
);

  wire [15:0] one_bit_shifter_right_1_out_3, one_bit_shifter_right_2_out_3, one_bit_shifter_right_3_out_3,
       one_bit_shifter_right_4_out_3, one_bit_shifter_right_5_out_3, one_bit_shifter_right_7_out_3;

  one_bit_shifter_right one_bit_shifter_right_1 (
    .in_1(Input_Data), .in_2(in_1[0]), .out_3(one_bit_shifter_right_1_out_3));
  one_bit_shifter_right one_bit_shifter_right_2 (
    .in_1(one_bit_shifter_right_7_out_3), .in_2(in_1[2]), .out_3(one_bit_shifter_right_2_out_3));
  one_bit_shifter_right one_bit_shifter_right_3 (
    .in_1(one_bit_shifter_right_5_out_3), .in_2(in_1[2]), .out_3(one_bit_shifter_right_3_out_3));
  one_bit_shifter_right one_bit_shifter_right_4 (
    .in_1(one_bit_shifter_right_1_out_3), .in_2(in_1[1]), .out_3(one_bit_shifter_right_4_out_3));
  one_bit_shifter_right one_bit_shifter_right_5 (
    .in_1(one_bit_shifter_right_2_out_3), .in_2(in_1[2]), .out_3(one_bit_shifter_right_5_out_3));
  one_bit_shifter_right one_bit_shifter_right_6 (
    .in_1(one_bit_shifter_right_3_out_3), .in_2(in_1[2]), .out_3(Output_Data));
  one_bit_shifter_right one_bit_shifter_right_7 (
    .in_1(one_bit_shifter_right_4_out_3), .in_2(in_1[1]), .out_3(one_bit_shifter_right_7_out_3));

  // Other names for the same wires on the sheet: ShiftEnable1 = in_1[0]; ShiftEnable2 = in_1[1];
  //   ShiftEnable4 = in_1[2]
endmodule
