// Logisim project old_cpu_in_folder.circ as structural Verilog: 6 circuits, main circuit main
module main (
  input  reset,
  input  [1:0] OpType,
  input  WE,
  input  [2:0] WriteReg,
  input  [2:0] ReadReg1,
  input  [2:0] ReadReg2
);

  wire clock_1_out;
  wire [15:0] alu_1_outputdata, registerfile_1_reg1contents, registerfile_1_reg2contents;

  RAM #(.addrWidth(16), .dataWidth(16), .trigger("high"), .databus("bibus")) ram_1 ();  // open: addr, we, oe, clk, din, dout
  Clock clock_1 (.out(clock_1_out));
  TTY tty_1 ();  // open: data, clk, we, clr
  Keyboard keyboard_1 ();  // open: clk, re, clr, avail, data
  Button button_1 ();  // open: out
  RegisterFile registerfile_1 (
    .clk(clock_1_out), .reset(reset), .WriteData(alu_1_outputdata), .RegWriteEnable(WE),
    .WritePort(WriteReg), .ReadReg1(ReadReg1), .ReadReg2(ReadReg2),
    .Reg1Contents(registerfile_1_reg1contents), .Reg2Contents(registerfile_1_reg2contents));
  alu alu_1 (
    .InputData1(registerfile_1_reg1contents), .InputData2(registerfile_1_reg2contents), .OpType(OpType),
    .OutputData(alu_1_outputdata));

  // Notes on the sheet:
  //   Button
  //   TTY
  //   Keyboard
endmodule

module singleRegister (
  input  [15:0] dataIn,
  input  clk,
  input  writeEnable,
  input  reset,
  output [15:0] out_5
);

  wire clk_t;

  buf and_1 (clk_t, writeEnable);  // AND_Gate
  D_Flip_Flop d_ff_1 (.D(dataIn[0]), .clk(clk_t), .Q(out_5[0]), .reset(reset));  // open: Qn, preset
  D_Flip_Flop d_ff_2 (.D(dataIn[1]), .clk(clk_t), .Q(out_5[1]), .reset(reset));  // open: Qn, preset
  D_Flip_Flop d_ff_3 (.D(dataIn[2]), .clk(clk_t), .Q(out_5[2]), .reset(reset));  // open: Qn, preset
  D_Flip_Flop d_ff_4 (.D(dataIn[3]), .clk(clk_t), .Q(out_5[3]), .reset(reset));  // open: Qn, preset
  D_Flip_Flop d_ff_5 (.D(dataIn[4]), .clk(clk_t), .Q(out_5[4]), .reset(reset));  // open: Qn, preset
  D_Flip_Flop d_ff_6 (.D(dataIn[5]), .clk(clk_t), .Q(out_5[5]), .reset(reset));  // open: Qn, preset
  D_Flip_Flop d_ff_7 (.D(dataIn[6]), .clk(clk_t), .Q(out_5[6]), .reset(reset));  // open: Qn, preset
  D_Flip_Flop d_ff_8 (.D(dataIn[7]), .clk(clk_t), .Q(out_5[7]), .reset(reset));  // open: Qn, preset
  D_Flip_Flop d_ff_9 (.D(dataIn[8]), .clk(clk_t), .Q(out_5[8]), .reset(reset));  // open: Qn, preset
  D_Flip_Flop d_ff_10 (.D(dataIn[9]), .clk(clk_t), .Q(out_5[9]), .reset(reset));  // open: Qn, preset
  D_Flip_Flop d_ff_11 (.D(dataIn[10]), .clk(clk_t), .Q(out_5[10]), .reset(reset));  // open: Qn, preset
  D_Flip_Flop d_ff_12 (.D(dataIn[11]), .clk(clk_t), .Q(out_5[11]), .reset(reset));  // open: Qn, preset
  D_Flip_Flop d_ff_13 (.D(dataIn[12]), .clk(clk_t), .Q(out_5[12]), .reset(reset));  // open: Qn, preset
  D_Flip_Flop d_ff_14 (.D(dataIn[13]), .clk(clk_t), .Q(out_5[13]), .reset(reset));  // open: Qn, preset
  D_Flip_Flop d_ff_15 (.D(dataIn[14]), .clk(clk_t), .Q(out_5[14]), .reset(reset));  // open: Qn, preset
  D_Flip_Flop d_ff_16 (.D(dataIn[15]), .clk(clk_t), .Q(out_5[15]), .reset(reset));  // open: Qn, preset

  // Other names for the same wires on the sheet: in0 = dataIn[0]; in1 = dataIn[1]; in2 = dataIn[2]; in3 = dataIn[3];
  //   in4 = dataIn[4]; in5 = dataIn[5]; in6 = dataIn[6]; in7 = dataIn[7]; in8 = dataIn[8]; in9 = dataIn[9];
  //   in10 = dataIn[10]; in11 = dataIn[11]; in12 = dataIn[12]; in13 = dataIn[13]; in14 = dataIn[14];
  //   in15 = dataIn[15]; out0 = out_5[0]; out1 = out_5[1]; out2 = out_5[2]; out3 = out_5[3]; out4 = out_5[4];
  //   out5 = out_5[5]; out6 = out_5[6]; out7 = out_5[7]; out8 = out_5[8]; out9 = out_5[9]; out10 = out_5[10];
  //   out11 = out_5[11]; out12 = out_5[12]; out13 = out_5[13]; out14 = out_5[14]; out15 = out_5[15]
endmodule

module RegisterFile (
  input  clk,
  input  reset,
  input  [15:0] WriteData,
  input  RegWriteEnable,
  input  [2:0] WritePort,
  input  [2:0] ReadReg1,
  input  [2:0] ReadReg2,
  output [15:0] Reg1Contents,
  output [15:0] Reg2Contents
);

  wire out1bit0, out1bit1, out1bit2, out1bit3, out1bit4, out1bit5, out1bit6, out1bit7, out2bit0, out2bit1,
       out2bit2, out2bit3, out2bit4, out2bit5, out2bit6, out2bit7, Write0, Write1, Write2, Write3, Write4,
       Write5, Write6, Write7;
  wire [15:0] singleregister_1_out_5, singleregister_2_out_5, singleregister_3_out_5, singleregister_4_out_5,
       singleregister_5_out_5, singleregister_6_out_5, singleregister_7_out_5, singleregister_8_out_5;

  Decoder #(.select(3)) decoder_1 (
    .out0(Write0), .out1(Write1), .out2(Write2), .out3(Write3), .out4(Write4), .out5(Write5), .out6(Write6),
    .out7(Write7), .sel(WritePort), .en(RegWriteEnable));
  Decoder #(.select(3)) decoder_2 (
    .out0(out1bit0), .out1(out1bit1), .out2(out1bit2), .out3(out1bit3), .out4(out1bit4), .out5(out1bit5),
    .out6(out1bit6), .out7(out1bit7), .sel(ReadReg1));  // open: en
  Decoder #(.select(3)) decoder_3 (
    .out0(out2bit0), .out1(out2bit1), .out2(out2bit2), .out3(out2bit3), .out4(out2bit4), .out5(out2bit5),
    .out6(out2bit6), .out7(out2bit7), .sel(ReadReg2));  // open: en
  Decoder #(.select(3)) decoder_4 (.out0(out1bit1));  // open: out1, out2, out3, out4, out5, out6, out7, sel, en
  singleRegister singleregister_1 (
    .dataIn(WriteData), .clk(clk), .writeEnable(Write0), .reset(reset), .out_5(singleregister_1_out_5));
  singleRegister singleregister_2 (
    .dataIn(WriteData), .clk(clk), .writeEnable(Write1), .reset(reset), .out_5(singleregister_2_out_5));
  singleRegister singleregister_3 (
    .dataIn(WriteData), .clk(clk), .writeEnable(Write2), .reset(reset), .out_5(singleregister_3_out_5));
  singleRegister singleregister_4 (
    .dataIn(WriteData), .clk(clk), .writeEnable(Write3), .reset(reset), .out_5(singleregister_4_out_5));
  singleRegister singleregister_5 (
    .dataIn(WriteData), .clk(clk), .writeEnable(Write4), .reset(reset), .out_5(singleregister_5_out_5));
  singleRegister singleregister_6 (
    .dataIn(WriteData), .clk(clk), .writeEnable(Write5), .reset(reset), .out_5(singleregister_6_out_5));
  singleRegister singleregister_7 (
    .dataIn(WriteData), .clk(clk), .writeEnable(Write6), .reset(reset), .out_5(singleregister_7_out_5));
  singleRegister singleregister_8 (
    .dataIn(WriteData), .clk(clk), .writeEnable(Write7), .reset(reset), .out_5(singleregister_8_out_5));
  assign Reg1Contents = out1bit0 ? singleregister_1_out_5 : 16'bz;  // Controlled_Buffer controlled_buffer_1
  assign Reg2Contents = out2bit0 ? singleregister_1_out_5 : 16'bz;  // Controlled_Buffer controlled_buffer_2
  assign Reg1Contents = out1bit1 ? singleregister_2_out_5 : 16'bz;  // Controlled_Buffer controlled_buffer_3
  assign Reg2Contents = out2bit1 ? singleregister_2_out_5 : 16'bz;  // Controlled_Buffer controlled_buffer_4
  assign Reg1Contents = out1bit2 ? singleregister_3_out_5 : 16'bz;  // Controlled_Buffer controlled_buffer_5
  assign Reg2Contents = out2bit2 ? singleregister_3_out_5 : 16'bz;  // Controlled_Buffer controlled_buffer_6
  assign Reg1Contents = out1bit3 ? singleregister_4_out_5 : 16'bz;  // Controlled_Buffer controlled_buffer_7
  assign Reg2Contents = out2bit3 ? singleregister_4_out_5 : 16'bz;  // Controlled_Buffer controlled_buffer_8
  assign Reg1Contents = out1bit4 ? singleregister_5_out_5 : 16'bz;  // Controlled_Buffer controlled_buffer_9
  assign Reg2Contents = out2bit4 ? singleregister_5_out_5 : 16'bz;  // Controlled_Buffer controlled_buffer_10
  assign Reg1Contents = out1bit5 ? singleregister_6_out_5 : 16'bz;  // Controlled_Buffer controlled_buffer_11
  assign Reg2Contents = out2bit5 ? singleregister_6_out_5 : 16'bz;  // Controlled_Buffer controlled_buffer_12
  assign Reg1Contents = out1bit6 ? singleregister_7_out_5 : 16'bz;  // Controlled_Buffer controlled_buffer_13
  assign Reg2Contents = out2bit6 ? singleregister_7_out_5 : 16'bz;  // Controlled_Buffer controlled_buffer_14
  assign Reg1Contents = out1bit7 ? singleregister_8_out_5 : 16'bz;  // Controlled_Buffer controlled_buffer_15
  assign Reg2Contents = out2bit7 ? singleregister_8_out_5 : 16'bz;  // Controlled_Buffer controlled_buffer_16
endmodule

module alu (
  input  [15:0] InputData1,
  input  [15:0] InputData2,
  input  [1:0] OpType,
  output [15:0] OutputData
);

  wire [15:0] not_1_out, or_1_out, sixteen_bit_adder_1_sum, sixteen_bit_adder_2_sum;

  assign not_1_out = ~InputData1;  // NOT_Gate not_1, 16 bits wide
  sixteen_bit_adder sixteen_bit_adder_1 (
    .Sub(1'b0), .A(InputData1), .B(InputData2), .Sum(sixteen_bit_adder_1_sum));  // open: Overflow
  sixteen_bit_adder sixteen_bit_adder_2 (
    .Sub(1'b1), .A(InputData1), .B(InputData2), .Sum(sixteen_bit_adder_2_sum));  // open: Overflow
  assign or_1_out = InputData2 | InputData1;  // OR_Gate or_1, 16 bits wide
  Multiplexer #(.select(2), .width(16), .enable("false")) multiplexer_1 (
    .in0(sixteen_bit_adder_1_sum), .in1(sixteen_bit_adder_2_sum), .in2(or_1_out), .in3(not_1_out),
    .out(OutputData), .sel(OpType));
endmodule

module one_bit_adder (
  input  C_in,
  input  A,
  input  B,
  output Sum,
  output C_out
);

  wire and_1_out, and_2_out, xor_1_out;

  and and_1 (and_1_out, A, B);
  xor xor_1 (xor_1_out, A, B);
  or or_1 (C_out, and_1_out, and_2_out);
  and and_2 (and_2_out, xor_1_out, C_in);
  xor xor_2 (Sum, C_in, xor_1_out);
endmodule

module sixteen_bit_adder (
  input  Sub,
  input  [15:0] A,
  input  [15:0] B,
  output Overflow,
  output [15:0] Sum
);

  wire one_bit_adder_1_c_out, one_bit_adder_2_c_out, one_bit_adder_3_c_out, one_bit_adder_4_c_out,
       one_bit_adder_5_c_out, one_bit_adder_6_c_out, one_bit_adder_7_c_out, one_bit_adder_8_c_out,
       one_bit_adder_9_c_out, one_bit_adder_10_c_out, one_bit_adder_11_c_out, one_bit_adder_12_c_out,
       one_bit_adder_13_c_out, one_bit_adder_14_c_out, one_bit_adder_15_c_out, one_bit_adder_16_c_out,
       xor_1_out, xor_2_out, xor_3_out, xor_4_out, xor_5_out, xor_6_out, xor_7_out, xor_8_out, xor_9_out,
       xor_10_out, xor_11_out, xor_12_out, xor_13_out, xor_14_out, xor_15_out, xor_16_out;

  xor xor_1 (xor_1_out, Sub, B[0]);
  one_bit_adder one_bit_adder_1 (.C_in(Sub), .A(xor_1_out), .B(A[0]), .Sum(Sum[0]), .C_out(one_bit_adder_1_c_out));
  xor xor_2 (xor_2_out, Sub, B[1]);
  one_bit_adder one_bit_adder_2 (
    .C_in(one_bit_adder_1_c_out), .A(xor_2_out), .B(A[1]), .Sum(Sum[1]), .C_out(one_bit_adder_2_c_out));
  xor xor_3 (xor_3_out, Sub, B[2]);
  one_bit_adder one_bit_adder_3 (
    .C_in(one_bit_adder_2_c_out), .A(xor_3_out), .B(A[2]), .Sum(Sum[2]), .C_out(one_bit_adder_3_c_out));
  xor xor_4 (xor_4_out, Sub, B[3]);
  one_bit_adder one_bit_adder_4 (
    .C_in(one_bit_adder_3_c_out), .A(xor_4_out), .B(A[3]), .Sum(Sum[3]), .C_out(one_bit_adder_4_c_out));
  xor xor_5 (xor_5_out, Sub, B[4]);
  one_bit_adder one_bit_adder_5 (
    .C_in(one_bit_adder_4_c_out), .A(xor_5_out), .B(A[4]), .Sum(Sum[4]), .C_out(one_bit_adder_5_c_out));
  xor xor_6 (xor_6_out, Sub, B[5]);
  one_bit_adder one_bit_adder_6 (
    .C_in(one_bit_adder_5_c_out), .A(xor_6_out), .B(A[5]), .Sum(Sum[5]), .C_out(one_bit_adder_6_c_out));
  xor xor_7 (xor_7_out, Sub, B[6]);
  one_bit_adder one_bit_adder_7 (
    .C_in(one_bit_adder_6_c_out), .A(xor_7_out), .B(A[6]), .Sum(Sum[6]), .C_out(one_bit_adder_7_c_out));
  xor xor_8 (xor_8_out, Sub, B[7]);
  one_bit_adder one_bit_adder_8 (
    .C_in(one_bit_adder_7_c_out), .A(xor_8_out), .B(A[7]), .Sum(Sum[7]), .C_out(one_bit_adder_8_c_out));
  xor xor_9 (xor_9_out, Sub, B[8]);
  one_bit_adder one_bit_adder_9 (
    .C_in(one_bit_adder_8_c_out), .A(xor_9_out), .B(A[8]), .Sum(Sum[8]), .C_out(one_bit_adder_9_c_out));
  xor xor_10 (xor_10_out, Sub, B[9]);
  one_bit_adder one_bit_adder_10 (
    .C_in(one_bit_adder_9_c_out), .A(xor_10_out), .B(A[9]), .Sum(Sum[9]), .C_out(one_bit_adder_10_c_out));
  xor xor_11 (xor_11_out, Sub, B[10]);
  one_bit_adder one_bit_adder_11 (
    .C_in(one_bit_adder_10_c_out), .A(xor_11_out), .B(A[10]), .Sum(Sum[10]), .C_out(one_bit_adder_11_c_out));
  xor xor_12 (xor_12_out, Sub, B[11]);
  one_bit_adder one_bit_adder_12 (
    .C_in(one_bit_adder_11_c_out), .A(xor_12_out), .B(A[11]), .Sum(Sum[11]), .C_out(one_bit_adder_12_c_out));
  xor xor_13 (xor_13_out, Sub, B[12]);
  one_bit_adder one_bit_adder_13 (
    .C_in(one_bit_adder_12_c_out), .A(xor_13_out), .B(A[12]), .Sum(Sum[12]), .C_out(one_bit_adder_13_c_out));
  xor xor_14 (xor_14_out, Sub, B[13]);
  one_bit_adder one_bit_adder_14 (
    .C_in(one_bit_adder_13_c_out), .A(xor_14_out), .B(A[13]), .Sum(Sum[13]), .C_out(one_bit_adder_14_c_out));
  xor xor_15 (xor_15_out, Sub, B[14]);
  one_bit_adder one_bit_adder_15 (
    .C_in(one_bit_adder_14_c_out), .A(xor_15_out), .B(A[14]), .Sum(Sum[14]), .C_out(one_bit_adder_15_c_out));
  xor xor_16 (xor_16_out, Sub, B[15]);
  one_bit_adder one_bit_adder_16 (
    .C_in(one_bit_adder_15_c_out), .A(xor_16_out), .B(A[15]), .Sum(Sum[15]), .C_out(one_bit_adder_16_c_out));
  xor xor_17 (Overflow, one_bit_adder_15_c_out, one_bit_adder_16_c_out);

  // Other names for the same wires on the sheet: s0 = Sum[0]; s1 = Sum[1]; s2 = Sum[2]; s3 = Sum[3]; s4 = Sum[4];
  //   s5 = Sum[5]; s6 = Sum[6]; s7 = Sum[7]; s8 = Sum[8]; s9 = Sum[9]; s10 = Sum[10]; s11 = Sum[11]; s12 = Sum[12];
  //   s13 = Sum[13]; s14 = Sum[14]; s15 = Sum[15]
endmodule
